// Logisim project leonardofalango.circ as structural Verilog
module HalfSum (
  input  a,
  input  b,
  output Sum,
  output CarryOut
);

  xor xor_1 (Sum, a, b);
  and and_1 (CarryOut, a, b);
endmodule

module FullSum (
  input  a,
  input  b,
  input  CarryIn,
  output Sum,
  output CarryOut
);

  wire halfsum_1_carryout, halfsum_1_sum, halfsum_2_carryout;

  HalfSum halfsum_1 (.a(a), .b(b), .Sum(halfsum_1_sum), .CarryOut(halfsum_1_carryout));
  HalfSum halfsum_2 (.a(halfsum_1_sum), .b(CarryIn), .Sum(Sum), .CarryOut(halfsum_2_carryout));
  or or_1 (CarryOut, halfsum_2_carryout, halfsum_1_carryout);
endmodule

module Sum (
  input  in_1,
  input  [15:0] in_2,
  input  [15:0] in_3,
  output [15:0] out_4,
  output CarryOut
);

  wire fullsum_1_carryout, fullsum_2_carryout, fullsum_3_carryout, fullsum_4_carryout, fullsum_5_carryout,
       fullsum_6_carryout, fullsum_7_carryout, fullsum_8_carryout, fullsum_9_carryout, fullsum_10_carryout,
       fullsum_11_carryout, fullsum_12_carryout, fullsum_13_carryout, fullsum_14_carryout,
       fullsum_15_carryout;

  FullSum fullsum_1 (.a(in_3[0]), .b(in_2[0]), .CarryIn(in_1), .Sum(out_4[0]), .CarryOut(fullsum_1_carryout));
  FullSum fullsum_2 (
    .a(in_3[1]), .b(in_2[1]), .CarryIn(fullsum_1_carryout), .Sum(out_4[1]), .CarryOut(fullsum_2_carryout));
  FullSum fullsum_3 (
    .a(in_3[2]), .b(in_2[2]), .CarryIn(fullsum_2_carryout), .Sum(out_4[2]), .CarryOut(fullsum_3_carryout));
  FullSum fullsum_4 (
    .a(in_3[3]), .b(in_2[3]), .CarryIn(fullsum_3_carryout), .Sum(out_4[3]), .CarryOut(fullsum_4_carryout));
  FullSum fullsum_5 (
    .a(in_3[4]), .b(in_2[4]), .CarryIn(fullsum_4_carryout), .Sum(out_4[4]), .CarryOut(fullsum_5_carryout));
  FullSum fullsum_6 (
    .a(in_3[5]), .b(in_2[5]), .CarryIn(fullsum_5_carryout), .Sum(out_4[5]), .CarryOut(fullsum_6_carryout));
  FullSum fullsum_7 (
    .a(in_3[6]), .b(in_2[6]), .CarryIn(fullsum_6_carryout), .Sum(out_4[6]), .CarryOut(fullsum_7_carryout));
  FullSum fullsum_8 (
    .a(in_3[7]), .b(in_2[7]), .CarryIn(fullsum_7_carryout), .Sum(out_4[7]), .CarryOut(fullsum_8_carryout));
  FullSum fullsum_9 (
    .a(in_3[8]), .b(in_2[8]), .CarryIn(fullsum_8_carryout), .Sum(out_4[8]), .CarryOut(fullsum_9_carryout));
  FullSum fullsum_10 (
    .a(in_3[9]), .b(in_2[9]), .CarryIn(fullsum_9_carryout), .Sum(out_4[9]), .CarryOut(fullsum_10_carryout));
  FullSum fullsum_11 (
    .a(in_3[10]), .b(in_2[10]), .CarryIn(fullsum_10_carryout), .Sum(out_4[10]), .CarryOut(fullsum_11_carryout));
  FullSum fullsum_12 (
    .a(in_3[11]), .b(in_2[11]), .CarryIn(fullsum_11_carryout), .Sum(out_4[11]), .CarryOut(fullsum_12_carryout));
  FullSum fullsum_13 (
    .a(in_3[12]), .b(in_2[12]), .CarryIn(fullsum_12_carryout), .Sum(out_4[12]), .CarryOut(fullsum_13_carryout));
  FullSum fullsum_14 (
    .a(in_3[13]), .b(in_2[13]), .CarryIn(fullsum_13_carryout), .Sum(out_4[13]), .CarryOut(fullsum_14_carryout));
  FullSum fullsum_15 (
    .a(in_3[14]), .b(in_2[14]), .CarryIn(fullsum_14_carryout), .Sum(out_4[14]), .CarryOut(fullsum_15_carryout));
  FullSum fullsum_16 (.a(in_3[15]), .b(in_2[15]), .CarryIn(fullsum_15_carryout), .Sum(out_4[15]), .CarryOut(CarryOut));

  // Other names for the same wires on the sheet: lucas = in_2[11]; joao = in_2[12]; roberto = in_2[13];
  //   leonardo = in_2[14]; carioca = in_2[15]; matheus = in_3[11]; jorge = in_3[12]; felipe = in_3[13];
  //   santos = in_3[14]; robson = in_3[15]
endmodule

module If (
  input  in_1,
  input  in_2,
  input  in_3
);

  wire and_1_out, and_2_out, not_1_out;

  not not_1 (not_1_out, in_2);
  and and_1 (and_1_out, in_1, not_1_out);
  and and_2 (and_2_out, in_2, in_3);
  // OR_Gate or_1 has open pins: in0=and_1_out, in1=and_2_out, out=open
endmodule

module ULA (
  input  [15:0] a,
  input  [15:0] b,
  input  [3:0] Operation,
  output [15:0] Result
);

  wire outEqual, outGreater, outLess;
  wire [15:0] outAnd, outDiv, outLeftShift, outMult, outNand, outOr, outRightShift, outShift, outSub, outSum,
       outXor;

  Multiplexer #(.select(4), .width(16)) multiplexer_1 (
    .in1(outMult), .in4(outDiv), .in5({{15{1'b0}}, outLess}), .in6(outRightShift), .in7(outSum),
    .in8({{15{1'b0}}, outEqual}), .in9(outNand), .in10(outSub), .in11({{15{1'b0}}, outGreater}),
    .in12(outXor), .in13(outShift), .in14(outOr), .in15(outAnd), .out(Result), .sel(Operation));  // open: in0, in2, in3, en
  Adder #(.width(16)) adder_1 (.a(a), .b(b), .out(outSum));  // open: cin, cout
  Subtractor #(.width(16)) subtractor_1 (.a(a), .b(b), .out(outSub));  // open: bin, bout
  Multiplier #(.width(16)) multiplier_1 (.a(a), .b(b), .out(outMult));  // open: cin, cout
  Divider #(.width(16)) divider_1 (.a(a), .b(b), .out(outDiv));  // open: upper, rem
  Shifter #(.width(16)) shifter_1 (.in(a), .\dist (b[3:0]), .out(outLeftShift));
  assign outAnd = a & b;  // AND_Gate and_1, 16 bits wide
  assign outOr = a | b;  // OR_Gate or_1, 16 bits wide
  assign outXor = a ^ b;  // XOR_Gate xor_1, 16 bits wide
  assign outNand = ~(a & b);  // NAND_Gate nand_1, 16 bits wide
  Shifter #(.width(16), .shift("lr")) shifter_2 (.in(a), .\dist (b[3:0]), .out(outRightShift));
  Comparator #(.width(16)) comparator_1 (.a(a), .b(b), .gt(outGreater), .eq(outEqual), .lt(outEqual));
endmodule
